# Fritzing sketch Esquema_elétrico_carrinho_Arduíno (saved by Fritzing 0.9.5d)
breadboards: 1

parts:
  Componente1 = Arduino Uno (Rev3)
  Componente2 = Bluetooth HC-05 Macho
  U1 = L9110 H-bridge module [part_number="L9110 H-bridge"]
  M1 = DC Motor
  M2 = DC Motor
  Bat1 = battery_holder_single_18650

nets:
  N1: Componente1.D9_PWM, U1.B-IA
  N2: Componente1.D10_PWM/SS, U1.B-IB
  GND: Componente1.GND, Componente2.GND, U1.GND, Bat1.+#0
  N3: Componente1.D0/RX, Componente2.TXD
  N4: Componente1.D1/TX, Componente2.RXD
  N5: Componente1.D5_PWM, U1.A-IA
  N6: Componente1.D6_PWM, U1.A-IB
  VCC: Componente1.5V, Componente2.VCC, U1.VCC
  N7: Componente1.VIN, Bat1.+#1
  N8: U1.MOTOR_A-A, M2.pin_2
  N9: U1.MOTOR_A-B, M2.pin_1
  N10: U1.MOTOR_B-A, M1.pin_1
  N11: U1.MOTOR_B-B, M1.pin_2

custom parts:
  battery_holder_single_18650: single 18650 battery holder
